// Logisim project lab5_Q1.circ as structural Verilog: 1 circuit, main circuit main
module main (
  input  C0,
  input  [3:0] in_2,
  input  [3:0] in_3,
  input  in_4,
  output C1,
  output C2,
  output C3
);

  wire and_1_out, and_2_out, and_3_out, and_4_out, and_5_out, and_6_out, and_7_out, and_8_out, and_9_out,
       and_10_out, G0_out, G1_out, G2_out, G3_out, P0_out, P1_out, P2_out, P3_out;
  wire [0:0] or_4_out;
  wire [3:0] S0_out;

  xor P0 (P0_out, in_2[0], in_3[0]);
  and G0 (G0_out, in_2[0], in_3[0]);
  xor P1 (P1_out, in_2[1], in_3[1]);
  and G1 (G1_out, in_2[1], in_3[0]);
  xor P2 (P2_out, in_2[2], in_3[2]);
  and G2 (G2_out, in_2[2], in_3[2]);
  xor P3 (P3_out, in_2[3], in_3[3]);
  and G3 (G3_out, in_2[3], in_3[3]);
  and and_1 (and_1_out, G0_out, P1_out);
  and and_2 (and_2_out, G1_out, P2_out);
  and and_3 (and_3_out, G2_out, P3_out);
  and and_4 (and_4_out, C0, P0_out, P1_out);
  and and_5 (and_5_out, G0_out, P1_out, P2_out);
  and and_6 (and_6_out, G1_out, P2_out, P3_out);
  and and_7 (and_7_out, C0, P0_out, P1_out, P2_out);
  and and_8 (and_8_out, G0_out, P1_out, P2_out, P3_out);
  and and_9 (and_9_out, C0, P0_out, P1_out, P2_out, P3_out);
  and and_10 (and_10_out, C0, P0_out);
  xor S0 (S0_out[0], P0_out, C0);
  or or_1 (C1, and_10_out, G0_out);
  xor S1 (S0_out[1], P1_out, G0_out);
  or or_2 (C2, and_1_out, and_4_out, G1_out);
  or or_3 (C3, and_2_out, and_5_out, and_7_out, G2_out);
  or or_4 (or_4_out[0], and_3_out, G3_out, and_6_out, and_8_out, and_9_out);
  xor S2 (S0_out[2], P2_out, C2);
  xor S4 (S0_out[3], P3_out, C3);
  Hex_Digit_Display hex_digit_display_1 (.value({{3{in_4}}, or_4_out[0]}));  // open: dp
  Hex_Digit_Display hex_digit_display_2 (.value(S0_out));  // open: dp
endmodule
